# Fritzing sketch design with simple soft latching circuit (saved by Fritzing 0.9.3b)
breadboards: 1

parts:
  SWT = SWITCH-MOMENTARY-2 [package=tactile-pth-12mm]
  D = Diode [package=diode-1n4148]
  P = Basic Force Sensing Resistor (FSR) [package=THT]
  BT = Bluetooth HC-05 Macho
  RF24 = NRF24L01+ Breakout Board
  Q1 = MOSFET-NCHANNEL [package=sot23-3]
  IMU = MPU-9250-half [form=male package=THT]
  R5 = Resistor [tolerance=±5% resistance=10k package="1206 [SMD]"]
  R4 = Resistor [tolerance=±5% resistance=10k package="1206 [SMD]"]
  D_2 = Diode [package=diode-1n4148]
  BZ = Piezo Speaker
  BAT = LIPO-1000mAh with pcb pins [package=lipo-1000]
  Arduino = BAT Arduino MKR1000

nets:
  N1: SWT.1, D.A, Arduino.D4_PWM
  N2: SWT.2, Q1.D, D_2.C, BAT.+
  N3: D.C, Q1.S, D_2.A, Arduino.BAT+
  VCC: P.pin_0, BT.VCC, RF24.VCC, IMU.VCC, Arduino.VCC
  N4: P.pin_1, R5.Pin_0, Arduino.A2
  N5: BT.TXD, Arduino.D13_RX
  N6: BT.RXD, Arduino.14_TX
  GND: BT.GND, RF24.GND, IMU.GND, R5.Pin_1, R4.Pin_1, BZ.pin1, BAT.-, Arduino.GND, Arduino.BAT-
  N7: RF24.CE, Arduino.D0
  N8: RF24.CS, Arduino.D1
  N9: RF24.SCK, Arduino.D9_SCK
  N10: RF24.MOSI, Arduino.D8_MOSI
  N11: RF24.MISO, Arduino.D10_MISO
  N12: Q1.G, R4.Pin_0, Arduino.A3
  N13: IMU.SCL, Arduino.D12_SCL
  N14: IMU.SDA, Arduino.D11_SDA
  N15: BZ.pin2, Arduino.A4

custom parts:
  MPU-9250-half: Acelerometro y Giroscopio MPU-9250 Board, extra piece broken to make it half and only using the upper 4 pins. Assumes pins are male (original pins are female)
  LIPO-1000mAh with pcb pins: 1000mAh Lipo-battery with pcb pins
  BAT Arduino MKR1000: MKR1000 is a powerful board that combines the functionality of the Zero and the Wi-Fi Shield. It is the ideal solution for makers wanting to design IoT projects with minimal previous experience in networking
