# Fritzing sketch razor (saved by Fritzing 0.9.3b)
breadboards: 1

parts:
  Part1 = Arduino MKR1000
  Part2 = Bluetooth HC-05 Macho
  GY1 = MPU-6050 Board GY-521 [form="♀ (female)" package=THT]
  U1 = LIPO-1000mAh [package=lipo-1000]  # not connected
  J1 = Basic Force Sensing Resistor (FSR) [package=THT]
  R1 = Resistor [tolerance=±5% resistance=10k package=THT]

nets:
  VCC: Part1.VCC, Part2.VCC, GY1.pin1, J1.pin_1
  GND: Part1.GND, Part2.GND, GY1.pin2, R1.Pin_1
  N1: Part1.D11_SDA, GY1.pin4
  N2: Part1.D12_SCL, GY1.pin3
  N3: Part1.D13_RX, Part2.TXD
  N4: Part1.A3, J1.pin_0, R1.Pin_0

custom parts:
  Arduino MKR1000: MKR1000 is a powerful board that combines the functionality of the Zero and the Wi-Fi Shield. It is the ideal solution for makers wanting to design IoT projects with minimal previous experience in networking
  MPU-6050 Board GY-521: Acelerometro y Giroscopio MPU-6050 Board GY-521
